# Fritzing sketch scheme (saved by Fritzing 0.9.3b)
breadboards: 1

parts:
  R1 = Photocell (LDR) [package=THT]
  DHT11_1 = DHT11 module
  R2 = Resistor [tolerance=±5% resistance=10k package="1206 [SMD]"]
  U1 = NodeMCU V1.0
  LED1 = LED - 5mm [color="Orange (605nm)" package="5 mm [THT]"]
  R3 = Resistor [tolerance=±5% resistance=220 package=THT]
  SG1 = Buzzer 12mm [package=buzzer-ccv]

nets:
  VCC: R1.pin_0, DHT11_1.VCC, U1.3V3
  N1: R1.pin_1, R2.Pin_0, U1.A0
  GND: DHT11_1.GND, R2.Pin_1, U1.GND, LED1.cathode, SG1.2
  N2: DHT11_1.DATA, U1.D1
  N3: U1.D3, SG1.1
  N4: LED1.anode, R3.Pin_1

custom parts:
  DHT11 module: DHT11 black pcb module
  NodeMCU V1.0: ESP8266 based NodeMCU
